// Logisim project clocktemplate.circ as structural Verilog: 9 circuits, main circuit FullClock
module LCD_Display (
  input  b3,
  input  b2,
  input  b1,
  input  b0,
  output f,
  output a,
  output b,
  output g,
  output e,
  output d,
  output c
);

  wire and_1_out, and_2_out, and_3_out, and_4_out, and_5_out, and_6_out, and_7_out, and_8_out, and_9_out,
       and_10_out, and_11_out, and_12_out, and_13_out, and_14_out, and_15_out, and_16_out, and_17_out,
       and_18_out, and_19_out, and_20_out, and_21_out, and_22_out, and_23_out, and_24_out, and_25_out,
       and_26_out, not_1_out, not_2_out, not_3_out, not_4_out, not_5_out, not_6_out, not_7_out, not_8_out,
       not_9_out, not_10_out, not_11_out, not_12_out, not_13_out, not_14_out, not_15_out, not_16_out,
       not_17_out, not_18_out, not_19_out, not_20_out, not_21_out, not_22_out, not_23_out, not_24_out,
       not_25_out, not_26_out, not_27_out, not_28_out, not_29_out, not_30_out, not_31_out, not_32_out,
       not_33_out, not_34_out, not_35_out, not_36_out, not_37_out, not_38_out, not_39_out;

  not not_1 (not_1_out, b3);
  not not_2 (not_2_out, b1);
  and and_1 (and_1_out, not_1_out, not_2_out, not_3_out);
  not not_3 (not_3_out, b0);
  not not_4 (not_4_out, b3);
  and and_2 (and_2_out, not_4_out, b2, not_5_out);
  not not_5 (not_5_out, b1);
  not not_6 (not_6_out, b3);
  and and_3 (and_3_out, not_6_out, b2, not_7_out);
  not not_7 (not_7_out, b0);
  not not_8 (not_8_out, b2);
  and and_4 (and_4_out, b3, not_8_out, not_9_out);
  not not_9 (not_9_out, b1);
  and and_5 (and_5_out, b3, b1, not_10_out);
  not not_10 (not_10_out, b0);
  not not_11 (not_11_out, b2);
  and and_6 (and_6_out, not_11_out, not_12_out);
  not not_12 (not_12_out, b0);
  not not_13 (not_13_out, b3);
  and and_7 (and_7_out, not_13_out, b1);
  and and_8 (and_8_out, b2, b0);
  and and_9 (and_9_out, b3, not_14_out);
  not not_14 (not_14_out, b1);
  not not_15 (not_15_out, b2);
  not not_16 (not_16_out, b1);
  and and_10 (and_10_out, not_16_out, not_17_out);
  not not_17 (not_17_out, b0);
  and and_11 (and_11_out, b1, b0);
  not not_18 (not_18_out, b3);
  and and_12 (and_12_out, not_18_out, not_19_out, b1);
  not not_19 (not_19_out, b2);
  and and_13 (and_13_out, b2, not_20_out);
  not not_20 (not_20_out, b1);
  and and_14 (and_14_out, b2, not_21_out);
  not not_21 (not_21_out, b0);
  and and_15 (and_15_out, b3, not_22_out);
  not not_22 (not_22_out, b1);
  not not_23 (not_23_out, b2);
  and and_16 (and_16_out, not_23_out, not_24_out);
  not not_24 (not_24_out, b0);
  not not_25 (not_25_out, b3);
  and and_17 (and_17_out, not_25_out, b1, not_26_out);
  not not_26 (not_26_out, b0);
  and and_18 (and_18_out, b3, not_27_out, not_28_out);
  not not_27 (not_27_out, b1);
  not not_28 (not_28_out, b0);
  not not_29 (not_29_out, b2);
  and and_19 (and_19_out, not_29_out, not_30_out);
  not not_30 (not_30_out, b0);
  not not_31 (not_31_out, b3);
  not not_32 (not_32_out, b2);
  and and_20 (and_20_out, not_31_out, not_32_out, b1);
  not not_33 (not_33_out, b3);
  and and_21 (and_21_out, not_33_out, b1, not_34_out);
  not not_34 (not_34_out, b0);
  and and_22 (and_22_out, b2, not_35_out, b0);
  not not_35 (not_35_out, b1);
  and and_23 (and_23_out, b3, not_36_out);
  not not_36 (not_36_out, b1);
  not not_37 (not_37_out, b3);
  and and_24 (and_24_out, not_37_out, not_38_out);
  not not_38 (not_38_out, b1);
  and and_25 (and_25_out, b2, b1);
  and and_26 (and_26_out, b3, not_39_out);
  not not_39 (not_39_out, b2);
  or or_1 (f, and_1_out, and_2_out, and_3_out, and_4_out, and_5_out);
  or or_2 (a, and_6_out, and_7_out, and_8_out, and_9_out);
  or or_3 (b, not_15_out, and_10_out, and_11_out, b3);
  or or_4 (g, and_12_out, and_13_out, and_14_out, and_15_out);
  or or_5 (e, and_16_out, and_17_out, and_18_out);
  or or_6 (d, and_19_out, and_20_out, and_21_out, and_22_out, and_23_out);
  or or_7 (c, and_24_out, b0, and_25_out, and_26_out);
endmodule

module Add4 (
  input  [3:0] A,
  input  [3:0] B,
  input  Cin,
  output [3:0] S,
  output Cout
);

  wire add1_1_s, add1_2_s, add1_3_s;

  Add1 add1_1 (.A(A[0]), .B(B[0]), .Cin(Cin), .S(add1_1_s), .Cout(S[0]));
  Add1 add1_2 (.A(A[1]), .B(B[1]), .Cin(add1_1_s), .S(add1_2_s), .Cout(S[1]));
  Add1 add1_3 (.A(A[2]), .B(B[2]), .Cin(add1_2_s), .S(add1_3_s), .Cout(S[2]));
  Add1 add1_4 (.A(A[3]), .B(B[3]), .Cin(add1_3_s), .S(Cout), .Cout(S[3]));
endmodule

module Add1 (
  input  A,
  input  B,
  input  Cin,
  output S,
  output Cout
);

  wire and_1_out, and_2_out, xor_1_out;

  xor xor_1 (xor_1_out, A, B);
  and and_1 (and_1_out, A, B);
  and and_2 (and_2_out, xor_1_out, Cin);
  xor xor_2 (Cout, xor_1_out, Cin);
  or or_1 (S, and_1_out, and_2_out);
endmodule

module FullClock (
  input  start
);

  wire clock_1_out, lcd_display_1_a, lcd_display_1_b, lcd_display_1_c, lcd_display_1_d, lcd_display_1_e,
       lcd_display_1_f, lcd_display_1_g, lcd_display_2_a, lcd_display_2_b, lcd_display_2_c, lcd_display_2_d,
       lcd_display_2_e, lcd_display_2_f, lcd_display_2_g, lcd_display_3_a, lcd_display_3_b, lcd_display_3_c,
       lcd_display_3_d, lcd_display_3_e, lcd_display_3_f, lcd_display_3_g, lcd_display_4_a, lcd_display_4_b,
       lcd_display_4_c, lcd_display_4_d, lcd_display_4_e, lcd_display_4_f, lcd_display_4_g, lcd_display_5_a,
       lcd_display_5_b, lcd_display_5_c, lcd_display_5_d, lcd_display_5_e, lcd_display_5_f, lcd_display_5_g,
       lcd_display_6_a, lcd_display_6_b, lcd_display_6_c, lcd_display_6_d, lcd_display_6_e, lcd_display_6_f,
       lcd_display_6_g, six_counter_1_cout, six_counter_2_cout, ten_counter_1_cout, ten_counter_2_cout;
  wire [3:0] hours_logic_1_ones_hour, hours_logic_1_tens_hour, six_counter_1_s, six_counter_2_s,
       ten_counter_1_s, ten_counter_2_s;

  Clock clock_1 (.out(clock_1_out));
  // Probe on six_counter_1_cout
  hours_logic hours_logic_1 (
    .Cin(six_counter_1_cout), .clk(clock_1_out), .ones_hour(hours_logic_1_ones_hour),
    .tens_hour(hours_logic_1_tens_hour));
  six_counter six_counter_1 (
    .Cin(ten_counter_1_cout), .clk(clock_1_out), .Cout(six_counter_1_cout), .S(six_counter_1_s));
  ten_counter ten_counter_1 (
    .Cin(six_counter_2_cout), .clk(clock_1_out), .Cout(ten_counter_1_cout), .S(ten_counter_1_s));
  six_counter six_counter_2 (
    .Cin(ten_counter_2_cout), .clk(clock_1_out), .Cout(six_counter_2_cout), .S(six_counter_2_s));
  ten_counter ten_counter_2 (.Cin(start), .clk(clock_1_out), .Cout(ten_counter_2_cout), .S(ten_counter_2_s));
  LCD_Display lcd_display_1 (
    .b3(hours_logic_1_tens_hour[3]), .b2(hours_logic_1_tens_hour[2]), .b1(hours_logic_1_tens_hour[1]),
    .b0(hours_logic_1_tens_hour[0]), .f(lcd_display_1_f), .a(lcd_display_1_a), .b(lcd_display_1_b),
    .g(lcd_display_1_g), .e(lcd_display_1_e), .d(lcd_display_1_d), .c(lcd_display_1_c));
  LCD_Display lcd_display_2 (
    .b3(hours_logic_1_ones_hour[3]), .b2(hours_logic_1_ones_hour[2]), .b1(hours_logic_1_ones_hour[1]),
    .b0(hours_logic_1_ones_hour[0]), .f(lcd_display_2_f), .a(lcd_display_2_a), .b(lcd_display_2_b),
    .g(lcd_display_2_g), .e(lcd_display_2_e), .d(lcd_display_2_d), .c(lcd_display_2_c));
  LCD_Display lcd_display_3 (
    .b3(six_counter_1_s[3]), .b2(six_counter_1_s[2]), .b1(six_counter_1_s[1]), .b0(six_counter_1_s[0]),
    .f(lcd_display_3_f), .a(lcd_display_3_a), .b(lcd_display_3_b), .g(lcd_display_3_g), .e(lcd_display_3_e),
    .d(lcd_display_3_d), .c(lcd_display_3_c));
  LCD_Display lcd_display_4 (
    .b3(ten_counter_1_s[3]), .b2(ten_counter_1_s[2]), .b1(ten_counter_1_s[1]), .b0(ten_counter_1_s[0]),
    .f(lcd_display_4_f), .a(lcd_display_4_a), .b(lcd_display_4_b), .g(lcd_display_4_g), .e(lcd_display_4_e),
    .d(lcd_display_4_d), .c(lcd_display_4_c));
  LCD_Display lcd_display_5 (
    .b3(six_counter_2_s[3]), .b2(six_counter_2_s[2]), .b1(six_counter_2_s[1]), .b0(six_counter_2_s[0]),
    .f(lcd_display_5_f), .a(lcd_display_5_a), .b(lcd_display_5_b), .g(lcd_display_5_g), .e(lcd_display_5_e),
    .d(lcd_display_5_d), .c(lcd_display_5_c));
  LCD_Display lcd_display_6 (
    .b3(ten_counter_2_s[3]), .b2(ten_counter_2_s[2]), .b1(ten_counter_2_s[1]), .b0(ten_counter_2_s[0]),
    .f(lcd_display_6_f), .a(lcd_display_6_a), .b(lcd_display_6_b), .g(lcd_display_6_g), .e(lcd_display_6_e),
    .d(lcd_display_6_d), .c(lcd_display_6_c));
  _7_Segment_Display u_7_segment_display_1 (
    .g(lcd_display_1_g), .f(lcd_display_1_f), .a(lcd_display_1_a), .b(lcd_display_1_b), .e(lcd_display_1_e),
    .d(lcd_display_1_d), .c(lcd_display_1_c));  // open: dp
  _7_Segment_Display u_7_segment_display_2 (
    .g(lcd_display_2_g), .f(lcd_display_2_f), .a(lcd_display_2_a), .b(lcd_display_2_b), .e(lcd_display_2_e),
    .d(lcd_display_2_d), .c(lcd_display_2_c));  // open: dp
  _7_Segment_Display u_7_segment_display_3 (
    .g(lcd_display_3_g), .f(lcd_display_3_f), .a(lcd_display_3_a), .b(lcd_display_3_b), .e(lcd_display_3_e),
    .d(lcd_display_3_d), .c(lcd_display_3_c));  // open: dp
  _7_Segment_Display u_7_segment_display_4 (
    .g(lcd_display_4_g), .f(lcd_display_4_f), .a(lcd_display_4_a), .b(lcd_display_4_b), .e(lcd_display_4_e),
    .d(lcd_display_4_d), .c(lcd_display_4_c));  // open: dp
  _7_Segment_Display u_7_segment_display_5 (
    .g(lcd_display_5_g), .f(lcd_display_5_f), .a(lcd_display_5_a), .b(lcd_display_5_b), .e(lcd_display_5_e),
    .d(lcd_display_5_d), .c(lcd_display_5_c));  // open: dp
  _7_Segment_Display u_7_segment_display_6 (
    .g(lcd_display_6_g), .f(lcd_display_6_f), .a(lcd_display_6_a), .b(lcd_display_6_b), .e(lcd_display_6_e),
    .d(lcd_display_6_d), .c(lcd_display_6_c));  // open: dp

  // Notes on the sheet:
  //   ones hour
  //   ones minute
  //   ones second
  //   tens hour
  //   tens minute
  //   tens second
endmodule

module ten_counter (
  input  Cin,
  input  clk,
  output Cout,
  output [3:0] S
);

  wire not_1_out, not_2_out, not_3_out, undriven;
  wire [3:0] add4_1_s, bit_extender_1_out, bit_extender_2_out, multiplexer_1_out;

  Register #(.width(4)) register_1 (.D(multiplexer_1_out), .clk(clk), .Q(S));  // open: en, clr
  assign bit_extender_1_out = {{3{1'b0}}, Cin};  // Bit_Extender bit_extender_1
  Add4 add4_1 (.A(bit_extender_1_out), .B(S), .Cin(undriven), .S(add4_1_s));  // open: Cout
  not not_1 (not_1_out, add4_1_s[0]);
  not not_2 (not_2_out, add4_1_s[2]);
  and and_1 (Cout, not_1_out, add4_1_s[1], not_2_out, add4_1_s[3]);
  not not_3 (not_3_out, Cout);
  Multiplexer #(.width(4), .enable("false")) multiplexer_1 (
    .in0(add4_1_s), .in1(bit_extender_2_out), .out(multiplexer_1_out), .sel(Cout));
  assign bit_extender_2_out = {{3{1'b0}}, not_3_out};  // Bit_Extender bit_extender_2
endmodule

module six_counter (
  input  Cin,
  input  clk,
  output Cout,
  output [3:0] S
);

  wire not_1_out, not_2_out, not_3_out;
  wire [3:0] add4_1_s, bit_extender_1_out, bit_extender_2_out, multiplexer_1_out;

  Register #(.width(4)) register_1 (.D(multiplexer_1_out), .clk(clk), .Q(S));  // open: en, clr
  assign bit_extender_1_out = {{3{1'b0}}, Cin};  // Bit_Extender bit_extender_1
  Add4 add4_1 (.A(bit_extender_1_out), .B(S), .S(add4_1_s));  // open: Cin, Cout
  not not_1 (not_1_out, add4_1_s[0]);
  not not_2 (not_2_out, add4_1_s[3]);
  and and_1 (Cout, not_1_out, add4_1_s[1], add4_1_s[2], not_2_out);
  not not_3 (not_3_out, Cout);
  Multiplexer #(.width(4), .enable("false")) multiplexer_1 (
    .in0(add4_1_s), .in1(bit_extender_2_out), .out(multiplexer_1_out), .sel(Cout));
  assign bit_extender_2_out = {{3{1'b0}}, not_3_out};  // Bit_Extender bit_extender_2
endmodule

module four_counter (
  input  Cin,
  input  clk,
  output Cout,
  output [3:0] S
);

  wire not_1_out, not_2_out, not_3_out, not_4_out;
  wire [3:0] add4_1_s, bit_extender_1_out, bit_extender_2_out, multiplexer_1_out;

  Register #(.width(4)) register_1 (.D(multiplexer_1_out), .clk(clk), .Q(S));  // open: en, clr
  assign bit_extender_1_out = {{3{1'b0}}, Cin};  // Bit_Extender bit_extender_1
  Add4 add4_1 (.A(bit_extender_1_out), .B(S), .S(add4_1_s));  // open: Cin, Cout
  not not_1 (not_1_out, add4_1_s[0]);
  not not_2 (not_2_out, add4_1_s[1]);
  not not_3 (not_3_out, add4_1_s[3]);
  and and_1 (Cout, not_1_out, not_2_out, add4_1_s[2], not_3_out);
  not not_4 (not_4_out, Cout);
  Multiplexer #(.width(4), .enable("false")) multiplexer_1 (
    .in0(add4_1_s), .in1(bit_extender_2_out), .out(multiplexer_1_out), .sel(Cout));
  assign bit_extender_2_out = {{3{1'b0}}, not_4_out};  // Bit_Extender bit_extender_2
endmodule

module three_counter (
  input  Cin,
  input  clk,
  output [3:0] S,
  output Cout
);

  wire not_1_out, not_2_out, not_3_out;
  wire [3:0] add4_1_s, bit_extender_1_out, bit_extender_2_out, multiplexer_1_out;

  Register #(.width(4)) register_1 (.D(multiplexer_1_out), .clk(clk), .Q(S));  // open: en, clr
  assign bit_extender_1_out = {{3{1'b0}}, Cin};  // Bit_Extender bit_extender_1
  Add4 add4_1 (.A(bit_extender_1_out), .B(S), .S(add4_1_s));  // open: Cin, Cout
  and and_1 (Cout, add4_1_s[0], add4_1_s[1], not_1_out, not_2_out);
  not not_1 (not_1_out, add4_1_s[2]);
  not not_2 (not_2_out, add4_1_s[3]);
  not not_3 (not_3_out, Cout);
  Multiplexer #(.width(4), .enable("false")) multiplexer_1 (
    .in0(add4_1_s), .in1(bit_extender_2_out), .out(multiplexer_1_out), .sel(Cout));
  assign bit_extender_2_out = {{3{1'b0}}, not_3_out};  // Bit_Extender bit_extender_2
endmodule

module hours_logic (
  input  Cin,
  input  clk,
  output [3:0] ones_hour,
  output [3:0] tens_hour
);

  wire and_1_out, and_2_out, and_3_out, four_counter_1_cout, multiplexer_1_out, not_1_out, not_2_out,
       not_3_out, not_4_out, ten_counter_1_cout;
  wire [3:0] four_counter_1_s, ten_counter_1_s;

  and and_1 (and_1_out, and_3_out, Cin);
  not not_1 (not_1_out, and_1_out);
  and and_2 (and_2_out, not_1_out, Cin);
  four_counter four_counter_1 (.Cin(and_1_out), .clk(clk), .Cout(four_counter_1_cout), .S(four_counter_1_s));
  ten_counter ten_counter_1 (.Cin(and_2_out), .clk(clk), .Cout(ten_counter_1_cout), .S(ten_counter_1_s));
  three_counter three_counter_1 (.Cin(multiplexer_1_out), .clk(clk), .S(tens_hour));  // open: Cout
  Multiplexer #(.enable("false")) multiplexer_1 (
    .in0(ten_counter_1_cout), .in1(four_counter_1_cout), .out(multiplexer_1_out), .sel(and_3_out));
  not not_2 (not_2_out, tens_hour[3]);
  Multiplexer #(.width(4), .enable("false")) multiplexer_2 (
    .in0(ten_counter_1_s), .in1(four_counter_1_s), .out(ones_hour), .sel(and_3_out));
  not not_3 (not_3_out, tens_hour[0]);
  and and_3 (and_3_out, not_3_out, tens_hour[1], not_4_out, not_2_out);
  not not_4 (not_4_out, tens_hour[2]);
endmodule
