// Logisim project traffic_light_controller.circ as structural Verilog: 2 circuits, main circuit main
module main (
  input  S,
  input  A,
  input  B,
  output NextState
);

  wire and_1_out, and_2_out, and_3_out, and_4_out, not_1_out, not_2_out, not_3_out, not_4_out, not_5_out,
       not_6_out;

  not not_1 (not_1_out, S);
  not not_2 (not_2_out, A);
  not not_3 (not_3_out, S);
  not not_4 (not_4_out, A);
  not not_5 (not_5_out, B);
  not not_6 (not_6_out, A);
  and and_1 (and_1_out, not_1_out, not_2_out, B);
  and and_2 (and_2_out, not_3_out, A, B);
  and and_3 (and_3_out, S, not_4_out, not_5_out);
  and and_4 (and_4_out, S, not_6_out, B);
  or or_1 (NextState, and_1_out, and_2_out, and_3_out, and_4_out);
endmodule

module FSM (
  input  A,
  input  B
);

  wire clock_1_out, main_1_nextstate, not_1_out, register_1_q;

  Clock clock_1 (.out(clock_1_out));
  Register #(.width(1)) register_1 (.D(main_1_nextstate), .clk(clock_1_out), .Q(register_1_q));  // open: en, clr
  not not_1 (not_1_out, register_1_q);
  LED EWLight (.in(register_1_q));
  LED NSLight (.in(not_1_out));
  main main_1 (.S(register_1_q), .A(A), .B(B), .NextState(main_1_nextstate));
endmodule
